# Fritzing sketch Smart Alarm (saved by Fritzing 1.0.4)
breadboards: 1

parts:
  J1 = STM32 Nucleo boards
  OLED_I2C1 = OLED 128x64 I2C Monochrome Display
  A1 = Wemos S2 Mini [part_number="WeMos D1 Mini Lite"]
  Keypad4x2 = Keypad Membran 4x4  # not connected
  S1 = SWITCH-MOMENTARY-2 [package=reed_switch_pth]  # not connected
  J2 = Piezo Speaker

nets:
  N1: J1.D2, J2.pin2
  N2: J1.D4, A1.Pin_1, A1.Pin_9
  5V: J1.5V, OLED_I2C1.VDD, A1.Pin_17, A1.Pin_25
  N3: J1.GND, A1.Pin_18, A1.Pin_26, J2.pin1
  N4: J1.PC9, OLED_I2C1.SCK, A1.Pin_24, A1.Pin_32
  N5: J1.PB8, OLED_I2C1.SDA, A1.Pin_23, A1.Pin_31
  N6: A1.Pin_2, A1.Pin_10
  N7: A1.Pin_3, A1.Pin_11
  N8: A1.Pin_4, A1.Pin_12
  N9: A1.Pin_5, A1.Pin_13
  N10: A1.Pin_6, A1.Pin_14
  N11: A1.Pin_7, A1.Pin_15
  N12: A1.Pin_8, A1.Pin_16
  N13: A1.Pin_19, A1.Pin_27
  N14: A1.Pin_20, A1.Pin_28
  N15: A1.Pin_21, A1.Pin_29
  N16: A1.Pin_22, A1.Pin_30

custom parts:
  Wemos S2 Mini: A mini wifi board based on the ESP32-S2FN4R2.
  Keypad Membran 4x4: Membrane Keypad 4x4 Matrix
